# Fritzing sketch morse (saved by Fritzing 0.8.0b)
breadboards: 1

parts:
  Part1 = Arduino Uno (Rev3)
  LED1 = LED - 5mm [color="Red (633nm)" package="5 mm [THT]"]
  J1 = Piezo Speaker
  R1 = Resistor [tolerance=±5% resistance=1k package=THT]

nets (from the schematic view):
  N1: Part1.GND, R1.Pin_1
  N2: Part1.D7, J1.pin1
  N3: LED1.cathode, R1.Pin_0
  N4: LED1.anode, J1.pin2
